# Fritzing sketch mega (saved by Fritzing 0.9.3b)
breadboards: 2

parts:
  Part2 = Arduino Mega ADK (Rev3)
  S2 = Momentary Switch [package=ksa_sealed_tac_switch]
  R3 = Resistor [tolerance=±5% resistance=100 package=THT]
  R4 = Resistor [tolerance=±5% resistance=10k package=THT]
  U1 = LCD-16X2 [package=lcd-16x2_noholes]  # not connected
  M2 = Niren can bus module [package=THT]
  R5 = Trimmer Potentiometer [maximum_resistance=10kΩ package=THT]
  R6 = Resistor [tolerance=±5% resistance=220 package="0603 [SMD]"]
  R7 = Resistor [tolerance=±5% resistance=120 package="2512 [SMD]"]
  R8 = Resistor [tolerance=±5% resistance=120 package="2512 [SMD]"]
  LED3 = smd LED [color="Green (565nm)" package="0603 [SMD]"]

nets:
  N1: Part2.GND, R4.Pin_0, M2.pin2, R5.leg1, LED3.anode
  N2: Part2.5V, S2.1, S2.3, M2.pin1, R5.leg2, R6.Pin_0
  N3: Part2.D2_PWM, M2.pin7
  N4: Part2.D22, S2.2, S2.4, R4.Pin_1
  N5: Part2.D24, R3.Pin_0
  N6: Part2.D50/MISO, M2.pin4
  N7: Part2.D51/MOSI, M2.pin5
  N8: Part2.D52/SCK, M2.pin6
  N9: Part2.D53/SS, M2.pin3
  N10: R3.Pin_1, LED3.cathode
  N11: M2.pin12, R7.Pin_0, R8.Pin_0
  N12: M2.pin13, R7.Pin_1, R8.Pin_1

custom parts:
  Niren can bus module: Niren can bus module availabe on ebay and others. Pcb view assumes that you unsolder the 7 pin header and resolder it on the bottom of the module to connect to the pcb. The two jumpers and the can bus connector remain on the top of the board and don't appear in pcb view.
