# Fritzing sketch uno (saved by Fritzing 0.9.3b)
breadboards: 2

parts:
  Part1 = Arduino Uno (Rev3) - ICSP
  S1 = Momentary Switch [package=ksa_sealed_tac_switch]
  R1 = Resistor [tolerance=±5% resistance=10k package=THT]
  R2 = Resistor [tolerance=±5% resistance=100 package=THT]
  M1 = Niren can bus module [package=THT]
  R7 = Resistor [tolerance=±5% resistance=120 package="2512 [SMD]"]
  R8 = Resistor [tolerance=±5% resistance=120 package="2512 [SMD]"]
  LED4 = smd LED [color="White (6500K)" package="0603 [SMD]"]

nets:
  N1: Part1.D10_PWM/SS, M1.pin3
  N2: Part1.D11_PWM/MOSI, M1.pin5
  N3: Part1.D12/MISO, M1.pin4
  N4: Part1.D13/SCK, M1.pin6
  N5: Part1.D2, M1.pin7
  N6: Part1.D3_PWM, S1.1, S1.3, R1.Pin_1
  N7: Part1.D4, R2.Pin_0
  N8: Part1.5V, S1.2, S1.4, M1.pin1
  N9: Part1.GND, M1.pin2, LED4.anode
  N10: R2.Pin_1, LED4.cathode
  N11: M1.pin12, R7.Pin_0, R8.Pin_0
  N12: M1.pin13, R7.Pin_1, R8.Pin_1

custom parts:
  Niren can bus module: Niren can bus module availabe on ebay and others. Pcb view assumes that you unsolder the 7 pin header and resolder it on the bottom of the module to connect to the pcb. The two jumpers and the can bus connector remain on the top of the board and don't appear in pcb view.
